# Fritzing sketch Bernardo e Athila (saved by Fritzing 0.9.3b)

parts:
  Módulo_Bluetooth_–_HC-05 = Bluetooth HC-05 Macho
  Arduino = Arduino Uno (Rev3)
  74HC595_-_1 = 74HC595 [package="DIP16 [THT]"]
  74HC595_-_2 = 74HC595 [package="DIP16 [THT]"]
  74HC595_-_3 = 74HC595 [package="DIP16 [THT]"]
  74HC595_-_4 = 74HC595 [package="DIP16 [THT]"]
  LED1 = smd LED [color="Red (633nm)" package="0603 [SMD]"]
  LED2 = smd LED [color="Red (633nm)" package="0603 [SMD]"]
  LED3 = smd LED [color="Red (633nm)" package="0603 [SMD]"]
  LED4 = smd LED [color="Red (633nm)" package="0603 [SMD]"]
  LED5 = smd LED [color="Red (633nm)" package="0603 [SMD]"]
  LED6 = smd LED [color="Red (633nm)" package="0603 [SMD]"]
  LED7 = smd LED [color="Red (633nm)" package="0603 [SMD]"]
  LED8 = smd LED [color="Red (633nm)" package="0603 [SMD]"]
  LED9 = smd LED [color="Red (633nm)" package="0603 [SMD]"]
  LED10 = smd LED [color="Red (633nm)" package="0603 [SMD]"]
  LED11 = smd LED [color="Red (633nm)" package="0603 [SMD]"]
  LED12 = smd LED [color="Red (633nm)" package="0603 [SMD]"]
  LED13 = smd LED [color="Red (633nm)" package="0603 [SMD]"]
  LED14 = smd LED [color="Red (633nm)" package="0603 [SMD]"]
  LED15 = smd LED [color="Red (633nm)" package="0603 [SMD]"]
  LED16 = smd LED [color="Red (633nm)" package="0603 [SMD]"]
  LED17 = smd LED [color="Red (633nm)" package="0603 [SMD]"]
  LED18 = smd LED [color="Red (633nm)" package="0603 [SMD]"]
  LED19 = smd LED [color="Red (633nm)" package="0603 [SMD]"]
  LED20 = smd LED [color="Red (633nm)" package="0603 [SMD]"]
  LED21 = smd LED [color="Red (633nm)" package="0603 [SMD]"]
  LED22 = smd LED [color="Red (633nm)" package="0603 [SMD]"]
  LED23 = smd LED [color="Red (633nm)" package="0603 [SMD]"]
  LED24 = smd LED [color="Red (633nm)" package="0603 [SMD]"]
  LED25 = smd LED [color="Red (633nm)" package="0603 [SMD]"]
  LED26 = smd LED [color="Red (633nm)" package="0603 [SMD]"]
  LED27 = smd LED [color="Red (633nm)" package="0603 [SMD]"]
  LED28 = smd LED [color="Red (633nm)" package="0603 [SMD]"]
  LED29 = smd LED [color="Red (633nm)" package="0603 [SMD]"]
  LED30 = smd LED [color="Red (633nm)" package="0603 [SMD]"]
  LED31 = smd LED [color="Red (633nm)" package="0603 [SMD]"]
  LED32 = smd LED [color="Red (633nm)" package="0603 [SMD]"]
  R3 = Resistor [tolerance=±5% resistance=470 package="0402 [SMD]"]
  R5 = Resistor [tolerance=±5% resistance=470 package="0402 [SMD]"]
  R6 = Resistor [tolerance=±5% resistance=470 package="0402 [SMD]"]
  R7 = Resistor [tolerance=±5% resistance=470 package="0402 [SMD]"]
  R8 = Resistor [tolerance=±5% resistance=470 package="0402 [SMD]"]
  R9 = Resistor [tolerance=±5% resistance=470 package="0402 [SMD]"]
  R10 = Resistor [tolerance=±5% resistance=470 package="0402 [SMD]"]
  R11 = Resistor [tolerance=±5% resistance=470 package="0402 [SMD]"]
  R12 = Resistor [tolerance=±5% resistance=470 package="0402 [SMD]"]
  R13 = Resistor [tolerance=±5% resistance=470 package="0402 [SMD]"]
  R14 = Resistor [tolerance=±5% resistance=470 package="0402 [SMD]"]
  R15 = Resistor [tolerance=±5% resistance=470 package="0402 [SMD]"]
  R16 = Resistor [tolerance=±5% resistance=470 package="0402 [SMD]"]
  R17 = Resistor [tolerance=±5% resistance=470 package="0402 [SMD]"]
  R18 = Resistor [tolerance=±5% resistance=470 package="0402 [SMD]"]
  R19 = Resistor [tolerance=±5% resistance=470 package="0402 [SMD]"]
  R20 = Resistor [tolerance=±5% resistance=470 package="0402 [SMD]"]
  R21 = Resistor [tolerance=±5% resistance=470 package="0402 [SMD]"]
  R22 = Resistor [tolerance=±5% resistance=470 package="0402 [SMD]"]
  R23 = Resistor [tolerance=±5% resistance=470 package="0402 [SMD]"]
  R24 = Resistor [tolerance=±5% resistance=470 package="0402 [SMD]"]
  R25 = Resistor [tolerance=±5% resistance=470 package="0402 [SMD]"]
  R26 = Resistor [tolerance=±5% resistance=470 package="0402 [SMD]"]
  R27 = Resistor [tolerance=±5% resistance=470 package="0402 [SMD]"]
  R28 = Resistor [tolerance=±5% resistance=470 package="0402 [SMD]"]
  R29 = Resistor [tolerance=±5% resistance=470 package="0402 [SMD]"]
  R30 = Resistor [tolerance=±5% resistance=470 package="0402 [SMD]"]
  R31 = Resistor [tolerance=±5% resistance=470 package="0402 [SMD]"]
  R32 = Resistor [tolerance=±5% resistance=470 package="0402 [SMD]"]
  R33 = Resistor [tolerance=±5% resistance=470 package="0402 [SMD]"]
  R34 = Resistor [tolerance=±5% resistance=470 package="0402 [SMD]"]
  R35 = Resistor [tolerance=±5% resistance=470 package="0402 [SMD]"]

nets:
  N1: Módulo_Bluetooth_–_HC-05.TXD, Arduino.D0/RX
  VCC: Módulo_Bluetooth_–_HC-05.VCC, Arduino.5V, 74HC595_-_1.MR, 74HC595_-_1.VCC, 74HC595_-_2.MR, 74HC595_-_2.VCC, 74HC595_-_3.MR, 74HC595_-_3.VCC, 74HC595_-_4.MR, 74HC595_-_4.VCC
  GND: Módulo_Bluetooth_–_HC-05.GND, Arduino.GND, 74HC595_-_1.GND, 74HC595_-_1.OE, 74HC595_-_2.GND, 74HC595_-_2.OE, 74HC595_-_3.GND, 74HC595_-_3.OE, 74HC595_-_4.GND, 74HC595_-_4.OE, LED1.cathode, LED2.cathode, LED3.cathode, LED4.cathode, LED5.cathode, LED6.cathode, LED7.cathode, LED8.cathode, LED9.cathode, LED10.cathode, LED11.cathode, LED12.cathode, LED13.cathode, LED14.cathode, LED15.cathode, LED16.cathode, LED17.cathode, LED18.cathode, LED19.cathode, LED20.cathode, LED21.cathode, LED22.cathode, LED23.cathode, LED24.cathode, LED25.cathode, LED26.cathode, LED27.cathode, LED28.cathode, LED29.cathode, LED30.cathode, LED31.cathode, LED32.cathode
  N2: Arduino.D2, 74HC595_-_1.DS
  N3: Arduino.D3_PWM, 74HC595_-_1.ST_CP, 74HC595_-_2.ST_CP, 74HC595_-_3.ST_CP, 74HC595_-_4.ST_CP
  N4: Arduino.D4, 74HC595_-_1.SH_CP, 74HC595_-_2.SH_CP, 74HC595_-_3.SH_CP, 74HC595_-_4.SH_CP
  N5: 74HC595_-_1.Q1, R5.Pin_0
  N6: 74HC595_-_1.Q2, R6.Pin_0
  N7: 74HC595_-_1.Q3, R7.Pin_0
  N8: 74HC595_-_1.Q4, R8.Pin_0
  N9: 74HC595_-_1.Q5, R9.Pin_0
  N10: 74HC595_-_1.Q6, R10.Pin_0
  N11: 74HC595_-_1.Q7, R11.Pin_0
  N12: 74HC595_-_1.Q7', 74HC595_-_2.DS
  N13: 74HC595_-_1.Q0, R3.Pin_0
  N14: 74HC595_-_2.Q1, R18.Pin_0
  N15: 74HC595_-_2.Q2, R12.Pin_0
  N16: 74HC595_-_2.Q3, R13.Pin_0
  N17: 74HC595_-_2.Q4, R17.Pin_0
  N18: 74HC595_-_2.Q5, R14.Pin_0
  N19: 74HC595_-_2.Q6, R15.Pin_0
  N20: 74HC595_-_2.Q7, R16.Pin_0
  N21: 74HC595_-_2.Q7', 74HC595_-_3.DS
  N22: 74HC595_-_2.Q0, R19.Pin_0
  N23: 74HC595_-_3.Q1, R23.Pin_0
  N24: 74HC595_-_3.Q2, R22.Pin_0
  N25: 74HC595_-_3.Q3, R25.Pin_0
  N26: 74HC595_-_3.Q4, R21.Pin_0
  N27: 74HC595_-_3.Q5, R27.Pin_0
  N28: 74HC595_-_3.Q6, R20.Pin_0
  N29: 74HC595_-_3.Q7, R24.Pin_0
  N30: 74HC595_-_3.Q7', 74HC595_-_4.DS
  N31: 74HC595_-_3.Q0, R26.Pin_0
  N32: 74HC595_-_4.Q1, R31.Pin_0
  N33: 74HC595_-_4.Q2, R30.Pin_0
  N34: 74HC595_-_4.Q3, R33.Pin_0
  N35: 74HC595_-_4.Q4, R29.Pin_0
  N36: 74HC595_-_4.Q5, R35.Pin_0
  N37: 74HC595_-_4.Q6, R28.Pin_0
  N38: 74HC595_-_4.Q7, R32.Pin_0
  N39: 74HC595_-_4.Q0, R34.Pin_0
  N40: LED1.anode, R3.Pin_1
  N41: LED2.anode, R5.Pin_1
  N42: LED3.anode, R6.Pin_1
  N43: LED4.anode, R7.Pin_1
  N44: LED5.anode, R8.Pin_1
  N45: LED6.anode, R9.Pin_1
  N46: LED7.anode, R10.Pin_1
  N47: LED8.anode, R11.Pin_1
  N48: LED9.anode, R19.Pin_1
  N49: LED10.anode, R15.Pin_1
  N50: LED11.anode, R13.Pin_1
  N51: LED12.anode, R16.Pin_1
  N52: LED13.anode, R17.Pin_1
  N53: LED14.anode, R18.Pin_1
  N54: LED15.anode, R14.Pin_1
  N55: LED16.anode, R12.Pin_1
  N56: LED17.anode, R23.Pin_1
  N57: LED18.anode, R24.Pin_1
  N58: LED19.anode, R26.Pin_1
  N59: LED20.anode, R22.Pin_1
  N60: LED21.anode, R21.Pin_1
  N61: LED22.anode, R27.Pin_1
  N62: LED23.anode, R25.Pin_1
  N63: LED24.anode, R20.Pin_1
  N64: LED25.anode, R31.Pin_1
  N65: LED26.anode, R32.Pin_1
  N66: LED27.anode, R34.Pin_1
  N67: LED28.anode, R30.Pin_1
  N68: LED29.anode, R29.Pin_1
  N69: LED30.anode, R35.Pin_1
  N70: LED31.anode, R33.Pin_1
  N71: LED32.anode, R28.Pin_1
